# Fritzing sketch SmartGas (saved by Fritzing 0.9.3b)

parts:
  U1 = ESP32S-HiLetgo [part_number=ESP32S-HiLetgo]
  Ventilador = Fan - Ventilador [package=THT]
  LED1 = RGB LED (com. cathode, rgb) [package="5 mm [THT]"]
  Servo = Basic Servo

nets:
  N1: U1.3.3, Ventilador.5V
  GND: U1.GND, Ventilador.GND, LED1.common_cathode, Servo.gnd
  VIN: U1.VIN, Servo.vcc
  N2: U1.GPIO18, Servo.pulse
  N3: U1.GPIO21, LED1.blue_anode
  N4: U1.GPIO22, LED1.green_anode
  N5: U1.GPIO23, LED1.red_anode

custom parts:
  ESP32S-HiLetgo: HiLetgo ESP-WROOM-32 ESP32 ESP-32S Development Board 2.4GHz Dual-Mode WiFi + Bluetooth Dual Cores Microcontroller The ESP32 integrated with Antenna switches, RF Balun, power amplifiers, low-noise amplifiers, filters, and management modules, and the entire solution occupies the least area of PCB. 2.4 GHz Wi-Fi plus Bluetooth dual-mode chip, with TSMC Ultra-low power consumption 40nm technology,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
  Fan - Ventilador: Ventilador de 2 pines, se encuentra comunmente en computadoras de escritorio
